# Fritzing sketch Wemos_DHT22_Levelshifter (saved by Fritzing 0.9.3b)
circuit board: 2.63193cm x 2.14604cm
breadboards: 1

parts:
  J1 = female pin header, 8 pins [form="♀ (female)"]
  J2 = female pin header, 8 pins [form="♀ (female)"]
  BSS138 = MOSFET-NCHANNEL [package=sot23-3]
  R2_10k = Resistor [tolerance=±5% resistance=10k package="1206 [SMD]"]
  R1_10k = Resistor [tolerance=±5% resistance=10k package="1206 [SMD]"]
  C1_100nF = Ceramic Capacitor [capacitance=100nF package="1206 [SMD, multilayer]"]
  DHT22 = female pin header, 4 pins [form="♀ (female)"]

nets:
  N1: J1.pin6, BSS138.G, R1_10k.Pin_0
  N2: J1.pin7, C1_100nF.1, DHT22.pin3, DHT22.pin4
  N3: J1.pin8, BSS138.D, R2_10k.Pin_1, C1_100nF.0, DHT22.pin1
  N4: J2.pin8, BSS138.S, R1_10k.Pin_1
  N5: R2_10k.Pin_0, DHT22.pin2
