# Fritzing sketch Wemos_Honeywell_19C (saved by Fritzing 0.9.3b)
circuit board: 2.63518cm x 2.1733cm
breadboards: 1

parts:
  19C200PA5K = female pin header, 4 pins [form="♀ (female)"]
  R1_15kΩ_1% = Resistor [tolerance=±1% resistance=15k package="1206 [SMD]"]
  R3_220Ω_1% = Resistor [tolerance=±1% resistance=220 package="1206 [SMD]"]
  R2_6_8kΩ_1% = Resistor [tolerance=±1% resistance=6.8k package="1206 [SMD]"]
  J3 = female pin header, 8 pins [form="♀ (female)"]
  J2 = female pin header, 8 pins [form="♀ (female)"]
  SCD7815BTG = Voltage Regulator [package=to220-igo]
  C1_10µF = Ceramic Capacitor [capacitance=10µF package="1206 [SMD, multilayer]"]

nets:
  N1: 19C200PA5K.pin1, 19C200PA5K.pin3, R3_220Ω_1%.Pin_1, J2.pin2, SCD7815BTG.GND, C1_10µF.1
  N2: 19C200PA5K.pin2, R1_15kΩ_1%.Pin_0
  N3: 19C200PA5K.pin4, SCD7815BTG.OUT
  N4: R1_15kΩ_1%.Pin_1, R2_6_8kΩ_1%.Pin_0, J3.pin2
  N5: R3_220Ω_1%.Pin_0, R2_6_8kΩ_1%.Pin_1
  N6: J2.pin1, SCD7815BTG.IN, C1_10µF.0

notes:
  5V
  GND
  D4
  D3
  D2
  D1
  RX
  TX
  3V3
  D8
  D7
  D6
  D5
  D0
  A0
  RST
  SCD7815
  19C200P5k
  S+
  V+
  OUT
  IN
